# Fritzing sketch pewpew-10.4 (saved by Fritzing 0.9.3b)
circuit board: 10cm x 8.24812cm
breadboards: 1

parts:
  U1 = QFN-32 [chip_label=SAMD21 package=QFN]
  X1a = mystery part, 8 pins [chip_label="LED Matrix"]
  X1b = mystery part, 8 pins [chip_label="LED Matrix"]
  X2 = USB Connectors [package=usb-microb]
  C1 = Ceramic Capacitor [capacitance=1µF package="0603 [SMD, multilayer]"]
  C2 = Ceramic Capacitor [capacitance=1µF package="0603 [SMD, multilayer]"]
  Pad1 = Pad [width=2.6000000000000001 height=2.6000000000000001 connect=center]
  J1 = female alternating pin header, 12 pins [form="♀ (female)"]
  + = female pin header, 1 pin [form="♀ (female)"]
  - = female pin header, 1 pin [form="♀ (female)"]
  o = SWITCH-MOMENTARY-2 [package=tactile_switch_tall]
  → = SWITCH-MOMENTARY-2 [package=tactile_switch_tall]
  ↓ = SWITCH-MOMENTARY-2 [package=tactile_switch_tall]
  ← = SWITCH-MOMENTARY-2 [package=tactile_switch_tall]
  x = SWITCH-MOMENTARY-2 [package=tactile_switch_tall]
  ↑ = SWITCH-MOMENTARY-2 [package=tactile_switch_tall]
  0N/0FF = SPST Switch [package=switch-spst-smd-a]

nets:
  N1: U1.1, J1.pin6
  N2: U1.2, J1.pin7
  N3: U1.3, J1.pin8
  N4: U1.4, J1.pin9
  N5: U1.5, J1.pin10
  R1: U1.6, X1b.pin8
  C4: U1.7, X1b.pin7
  C6: U1.8, X1b.pin6, ↑.2
  3.3V: U1.9, U1.30, C1.0, J1.pin11, J1.pin12, 0N/0FF.P, 0N/0FF.S
  GND: U1.10, U1.28, X2.GND, C1.1, C2.1, Pad1.pad, J1.pin2, J1.pin3, -.pin1
  BUTTONS: U1.11, o.2, →.2, ↓.2, ←.2, x.2, ↑.1
  R4: U1.12, X1b.pin5
  C1: U1.13, X1b.pin4, →.1
  R2: U1.14, X1b.pin3
  C7: U1.15, X1b.pin2, ←.1
  C8: U1.16, X1b.pin1, ↓.1
  R5: U1.17, X1a.pin1
  R7: U1.18, X1a.pin2
  C2: U1.19, X1a.pin3, x.1
  C3: U1.20, X1a.pin4, o.1
  R8: U1.21, X1a.pin5
  C5: U1.22, X1a.pin6
  N6: U1.23, X2.D-
  N7: U1.24, X2.D+
  R6: U1.25, X1a.pin7
  RST: U1.26, J1.pin1
  R3: U1.27, X1a.pin8
  N8: U1.29, C2.0
  SWC: U1.31, J1.pin4
  SWD: U1.32, J1.pin5
  N9: +.pin1, 0N/0FF.O

notes:
  1
  R - - 1 2 3 4 5 6 7 + +3V
  PewPew 10.3 http://pewpew.rtfd.io
  PewPew, 10.4
